// Logisim project control-logic.circ as structural Verilog: 1 circuit, main circuit control_logic
module control_logic (
  input  [31:0] Instruction,
  input  BrEq,
  input  BrLt,
  output PCSel,
  output RegWEn,
  output [2:0] ImmSel,
  output BrUn,
  output ASel,
  output BSel,
  output [3:0] ALUSel,
  output MemWEn,
  output [1:0] WBSel
);

  wire and_1_out, comparator_2_eq, comparator_4_eq;
  wire [2:0] bit_extender_1_out;
  wire [3:0] multiplexer_1_out;
  wire [15:0] rom_1_data;

  Comparator #(.mode("unsigned"), .width(7)) comparator_1 (
    .a(Instruction[6:0]), .b(7'b0010011), .eq(RegWEn));  // open: gt, lt
  Comparator #(.mode("unsigned"), .width(7)) comparator_2 (
    .a(Instruction[31:25]), .b(7'b0100000), .eq(comparator_2_eq));  // open: gt, lt
  Comparator #(.mode("unsigned"), .width(7)) comparator_3 (.b(7'b0110011), .eq(RegWEn));  // open: a, gt, lt
  ROM #(.addrWidth(6), .dataWidth(16)) rom_1 (.data(rom_1_data));  // open: addr
  assign bit_extender_1_out = {{2{RegWEn}}, RegWEn};  // Bit_Extender bit_extender_1
  Comparator #(.mode("unsigned"), .width(3)) comparator_4 (
    .a(Instruction[14:12]), .b(3'b000), .eq(comparator_4_eq));  // open: gt, lt
  assign ImmSel = ~bit_extender_1_out;  // NOT_Gate not_1, 3 bits wide
  Multiplexer #(.width(4)) multiplexer_1 (.in0(4'b1101), .in1(4'b1100), .out(multiplexer_1_out), .sel(and_1_out));
  and and_1 (and_1_out, comparator_2_eq, comparator_4_eq);

  assign ALUSel[2:0] = Instruction[14:12];
  assign BSel = 1'b1;

  // Other names for the same wires on the sheet: func3[2:0] = Instruction[14:12]; OpCode[6:0] = Instruction[6:0];
  //   func7[6:0] = Instruction[31:25]

  // Notes on the sheet:
  //   INPUTS to your circuit
  //   Connect ROM Input here ->
  //   ROM FOR CONTROL LOGIC
  //   DON'T CHANGE THE LOCATIONS OF THE INPUTS AND OUTPUTS!
  //   This is only if you choose to do the ROM option
  //   CONNECT
  //   WIRE
  //   TO
  //   USE
  //   ROM
  //   OUTPUT from your circuit
  //   Reminder: If using ROM, use combinational logic for PCSel
endmodule
